# Fritzing sketch APDS-9960_Multi-VL53L1X (saved by Fritzing 0.9.3b)

parts:
  Bauteil1 = Arduino Nano (Rev3.0)
  Bauteil2 = Adafruit 4-channel I2C-safe Bi-directional Logic Level Converter [part_number="Adafruit #757"]
  Bauteil3 = Adafruit VL53L0X Time of Flight Distance Sensor [part_number="Adafruit #3317"]
  Bauteil4 = Adafruit VL53L0X Time of Flight Distance Sensor [part_number="Adafruit #3317"]
  Bauteil5 = Adafruit VL53L0X Time of Flight Distance Sensor [part_number="Adafruit #3317"]
  Bauteil6 = Adafruit APDS-9960 [part_number="Adafruit #3595"]

nets:
  N1: Bauteil1.D2, Bauteil2.B2
  N2: Bauteil1.D4, Bauteil3.XSHUT
  N3: Bauteil1.D5, Bauteil4.XSHUT
  N4: Bauteil1.D6, Bauteil5.XSHUT
  GND: Bauteil1.GND, Bauteil2.GND, Bauteil3.GND, Bauteil4.GND, Bauteil5.GND, Bauteil6.GND
  N5: Bauteil1.5V, Bauteil2.HV
  N6: Bauteil1.A5, Bauteil2.B4
  N7: Bauteil1.A4, Bauteil2.B3
  N8: Bauteil2.A4, Bauteil3.SCL, Bauteil4.SCL, Bauteil5.SCL, Bauteil6.SCL
  N9: Bauteil2.A3, Bauteil3.SDA, Bauteil4.SDA, Bauteil5.SDA, Bauteil6.SDA
  N10: Bauteil2.A2, Bauteil6.INT
  VIN: Bauteil2.LV, Bauteil3.VIN, Bauteil4.VIN, Bauteil5.VIN, Bauteil6.VIN

notes:
  Assume VL53L1X

custom parts:
  Adafruit 4-channel I2C-safe Bi-directional Logic Level Converter: Because the Arduino (and Basic Stamp) are 5V devices, and most modern sensors, displays, flash cards and modes are 3.3V-only, many makers find that they need to perform level shifting/conversion to protect the 3.3V device from 5V. We do have some other handy level shifters in the shop, from the DIP 74LVC245 to the fancy bi-directional TXB0108. However, neither of these are happy to work with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
  Adafruit VL53L0X Time of Flight Distance Sensor: The VL53L0X is a Time of Flight distance sensor like no other you've used! The sensor contains a very tiny invisible laser source, and a matching sensor. The VL53L0X can detect the "time of flight", or how long the light has taken to bounce back to the sensor. Since it uses a very narrow light source, it is good for determining distance of only the surface directly in front of it. Unlike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
  Adafruit APDS-9960: The APDS9960 from Avago Technologies has an integrated IR LED and driver, along with four directional photodiodes that sense reflected IR energy from the LED. It's proximity detection feature allows it to measure the distance an object is from the front of the sensor (up to a few centimeters) with 8 bit resolution. Since there are four IR sensors, you can measure the changes in light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
